// Logisim project BigASM.circ as structural Verilog
module BOARD_BIG_ASM (
  output out_1
);

  wire button_1_out, CLK, CLR, d_ff_1_q, not_1_out, Write, Write_ASCII;
  wire [6:0] ASCII;
  wire [7:0] counter_1_q;
  wire [23:0] Dir_INPUT, Dir_MEMORY;
  wire [31:0] INPUT, MEMORY_IN, MEMORY_OUT;

  Button button_1 (.out(button_1_out));
  Clock clock_1 (.out(CLK));
  D_Flip_Flop d_ff_1 (.clk(CLK), .D(1'b1), .Q(d_ff_1_q), .reset(button_1_out));  // open: Qn, preset, en
  D_Flip_Flop d_ff_2 (.clk(CLK), .D(d_ff_1_q), .Qn(CLR), .reset(button_1_out));  // open: Q, preset, en
  BIG_ASM big_asm_1 (
    .DATA_INPUT(INPUT), .MEMORY_IN(MEMORY_OUT), .CLK(CLK), .CLR(CLR), .DIR_INPUT(Dir_INPUT),
    .MEMORY_OUT(MEMORY_IN), .DIR_MEMORY(Dir_MEMORY), .Write_OUTPUT(Write), .ASCII(ASCII),
    .Write_ASCII(Write_ASCII), .END(out_1));
  MEMORY memory_1 (.DIR(Dir_MEMORY), .DATA_IN(MEMORY_IN), .WRITE(Write), .CLK(CLK), .CLR(CLR), .DATA_OUT(MEMORY_OUT));
  INPUT input_1 (.DIR(Dir_INPUT), .CLK(CLK), .DATA_OUT(INPUT));
  Counter counter_1 (.load(1'b0), .count(not_1_out), .Q(counter_1_q), .clk(CLK), .clr(CLR));  // open: D, carry
  not not_1 (not_1_out, out_1);
  // Probe on counter_1_q
  TTY #(.rows(32), .cols(60)) tty_1 (.data(ASCII), .clk(CLK), .we(Write_ASCII), .clr(CLR));

  // Other names for the same wires on the sheet: END = out_1

  // Notes on the sheet:
  //   COUNTER
  //   BOARD
endmodule

module INPUT (
  input  [23:0] DIR,
  input  CLK,
  output [31:0] DATA_OUT
);

  RAM #(.addrWidth(24), .dataWidth(32)) ram_1 (.addr(DIR), .data(DATA_OUT), .clk(CLK), .ld(1'b1));  // open: sel, clr
endmodule

module MEMORY (
  input  [23:0] DIR,
  input  [31:0] DATA_IN,
  input  WRITE,
  input  CLK,
  input  CLR,
  output [31:0] DATA_OUT
);

  RAM #(.addrWidth(24), .dataWidth(32), .bus("separate")) ram_1 (
    .addr(DIR), .din(DATA_IN), .data(DATA_OUT), .str(WRITE), .clk(CLK), .clr(CLR));  // open: sel, ld
endmodule

module BIG_ASM (
  input  [31:0] DATA_INPUT,
  input  [31:0] MEMORY_IN,
  input  CLK,
  input  CLR,
  output [23:0] DIR_INPUT,
  output [31:0] MEMORY_OUT,
  output [23:0] DIR_MEMORY,
  output Write_OUTPUT,
  output [6:0] ASCII,
  output Write_ASCII,
  output END
);

  ASM asm_1 (
    .in_1(CLK), .in_2(CLR), .Input_In(DATA_INPUT), .END(END), .Input_Address(DIR_INPUT),
    .Write_2(Write_ASCII), .ASCII(ASCII), .Memory_In(MEMORY_IN), .Write(Write_OUTPUT), .Address(DIR_MEMORY),
    .Memory_Out(MEMORY_OUT));

  // Other names for the same wires on the sheet: MemoryIn[31:0] = MEMORY_IN; MemoryOut[31:0] = MEMORY_OUT;
  //   WriteAddress[23:0] = DIR_MEMORY; WriteMemory = Write_OUTPUT
endmodule

module PRINT_UDEC (
  input  [31:0] num,
  input  start,
  input  CLK,
  input  RST,
  output [6:0] ASCII,
  output Write_ASCII,
  output \end 
);

  wire _0_c, _0_n, demultiplexer_1_out0, demultiplexer_2_out0, demultiplexer_2_out1, demultiplexer_3_out0,
       demultiplexer_3_out1, IDLE_2_q, IDLE_3_q, IDLE_4_q, IDLE_q, Lc, Lc_0, Ln, Ln_0, or_1_out;
  wire [23:0] bit_extender_1_out;
  wire [31:0] c, c___1, c___1_t, divider_1_rem, memory_1_data_out, multiplexer_1_out, multiplexer_2_out,
       multiplexer_3_out, n, n___10, n___10___48;

  Multiplexer #(.width(32), .enable("false")) multiplexer_1 (
    .in0(num), .in1(n___10), .out(multiplexer_1_out), .sel(Lc_0));
  Divider #(.width(32)) divider_1 (.a(n), .b(32'ha), .out(n___10), .rem(divider_1_rem));  // open: upper
  Adder #(.width(32)) adder_1 (.a(divider_1_rem), .b(32'h30), .out(n___10___48));  // open: cin, cout
  or or_1 (or_1_out, demultiplexer_1_out0, \end );
  Register #(.width(32)) u_n (.D(multiplexer_1_out), .en(Ln), .Q(n), .clk(CLK), .clr(RST));
  D_Flip_Flop IDLE (.clk(CLK), .D(or_1_out), .Q(IDLE_q), .preset(RST));  // open: Qn, en, reset
  Demultiplexer #(.enable("false")) demultiplexer_1 (
    .out0(demultiplexer_1_out0), .out1(Ln_0), .in(IDLE_q), .sel(start));
  or or_2 (Write_ASCII, demultiplexer_3_out0, demultiplexer_2_out1);
  Multiplexer #(.width(32), .enable("false")) multiplexer_2 (
    .in0(c___1), .in1(c___1_t), .out(multiplexer_2_out), .sel(Write_ASCII));
  Adder #(.width(32)) adder_2 (.a(c), .b(32'h1), .out(c___1));  // open: cin, cout
  Subtractor #(.width(32)) subtractor_1 (.a(c), .b(32'h1), .out(c___1_t));  // open: bin, bout
  D_Flip_Flop IDLE_2 (.clk(CLK), .D(Ln_0), .Q(IDLE_2_q), .reset(RST));  // open: Qn, preset, en
  Register #(.width(32)) u_c (.D(multiplexer_2_out), .en(Lc), .Q(c), .clk(CLK), .clr(RST));
  or or_3 (Lc_0, IDLE_2_q, demultiplexer_3_out1);
  Multiplexer #(.width(32), .enable("false")) multiplexer_3 (
    .in0(c), .in1(c___1_t), .out(multiplexer_3_out), .sel(Write_ASCII));
  Comparator #(.width(32), .mode("unsigned")) comparator_1 (.a({32{1'b0}}), .b(n), .lt(_0_n));  // open: gt, eq
  Comparator #(.width(32), .mode("unsigned")) comparator_2 (.a({32{1'b0}}), .b(c), .lt(_0_c));  // open: gt, eq
  D_Flip_Flop IDLE_3 (.clk(CLK), .D(Write_ASCII), .Q(IDLE_3_q), .reset(RST));  // open: Qn, preset, en
  Demultiplexer #(.enable("false")) demultiplexer_2 (
    .out0(demultiplexer_2_out0), .out1(demultiplexer_2_out1), .in(IDLE_3_q), .sel(_0_c));
  Bit_Extender #(.in_width(32), .out_width(24)) bit_extender_1 (.in(multiplexer_3_out), .out(bit_extender_1_out));
  D_Flip_Flop IDLE_4 (.clk(CLK), .D(Lc_0), .Q(IDLE_4_q), .reset(RST));  // open: Qn, preset, en
  or or_4 (Lc, Lc_0, Write_ASCII);
  or or_5 (Ln, Ln_0, Lc_0);
  Demultiplexer #(.enable("false")) demultiplexer_3 (
    .out0(demultiplexer_3_out0), .out1(demultiplexer_3_out1), .in(IDLE_4_q), .sel(_0_n));
  D_Flip_Flop IDLE_5 (.clk(CLK), .D(demultiplexer_2_out0), .Q(\end ), .reset(RST));  // open: Qn, preset, en
  MEMORY memory_1 (
    .DIR(bit_extender_1_out), .DATA_IN(n___10___48), .WRITE(Lc_0), .CLK(CLK), .CLR(RST),
    .DATA_OUT(memory_1_data_out));
  Bit_Extender #(.in_width(32), .out_width(7)) bit_extender_2 (.in(memory_1_data_out), .out(ASCII));

  // Other names for the same wires on the sheet: Lc_1 = Write_ASCII; Sc = Write_ASCII; Ln_1 = Lc_0; Sn = Lc_0;
  //   Write = Lc_0
endmodule

module PRINT_DEC (
  input  [31:0] num,
  input  start,
  input  CLK,
  input  RST,
  output [6:0] ASCII,
  output Write_ASCII,
  output END
);

  wire demultiplexer_1_out0, demultiplexer_1_out1, demultiplexer_2_out0, demultiplexer_3_out0, end_t,
       IDLE_3_q, IDLE_q, or_1_out, or_2_out, or_3_out, S_ASCII, startUDEC, Write_ASCII_1;
  wire [6:0] ASCII_t;
  wire [31:0] multiplexer_1_out, negator_1_out;

  or or_1 (or_1_out, demultiplexer_1_out0, END);
  Negator #(.width(32)) negator_1 (.in(num), .out(negator_1_out));
  D_Flip_Flop IDLE (.clk(CLK), .D(or_1_out), .Q(IDLE_q), .preset(RST));  // open: Qn, en, reset
  Demultiplexer #(.enable("false")) demultiplexer_1 (
    .out0(demultiplexer_1_out0), .out1(demultiplexer_1_out1), .in(IDLE_q), .sel(start));
  Multiplexer #(.width(32), .enable("false")) multiplexer_1 (
    .in0(num), .in1(negator_1_out), .out(multiplexer_1_out), .sel(num[31]));
  Demultiplexer #(.enable("false")) demultiplexer_2 (
    .out0(demultiplexer_2_out0), .out1(S_ASCII), .in(demultiplexer_1_out1), .sel(num[31]));
  or or_2 (or_2_out, demultiplexer_2_out0, S_ASCII);
  D_Flip_Flop IDLE_2 (.clk(CLK), .D(or_2_out), .Q(startUDEC), .reset(RST));  // open: Qn, preset, en
  PRINT_UDEC print_udec_1 (
    .num(multiplexer_1_out), .start(startUDEC), .CLK(CLK), .RST(RST), .ASCII(ASCII_t),
    .Write_ASCII(Write_ASCII_1), .\end (end_t));
  D_Flip_Flop IDLE_3 (.clk(CLK), .D(or_3_out), .Q(IDLE_3_q), .reset(RST));  // open: Qn, preset, en
  or or_3 (or_3_out, startUDEC, demultiplexer_3_out0);
  Demultiplexer #(.enable("false")) demultiplexer_3 (
    .out0(demultiplexer_3_out0), .out1(END), .in(IDLE_3_q), .sel(end_t));
  Multiplexer #(.width(7), .enable("false")) multiplexer_2 (
    .in0(ASCII_t), .in1(7'b0101101), .out(ASCII), .sel(S_ASCII));
  or or_4 (Write_ASCII, S_ASCII, Write_ASCII_1);

  // Other names for the same wires on the sheet: sign = num[31]; Write_ASCII_0 = S_ASCII
endmodule

module TEST_PRINT (
  input  [31:0] in_1,
  output out_2
);

  wire button_1_out, button_2_out, CLK, CLR, d_ff_1_q, Write_ASCII;
  wire [6:0] ASCII;

  Button button_1 (.out(button_1_out));
  Clock clock_1 (.out(CLK));
  D_Flip_Flop d_ff_1 (.clk(CLK), .D(1'b1), .Q(d_ff_1_q), .reset(button_1_out));  // open: Qn, preset, en
  D_Flip_Flop d_ff_2 (.clk(CLK), .D(d_ff_1_q), .Qn(CLR), .reset(button_1_out));  // open: Q, preset, en
  Button button_2 (.out(button_2_out));
  PRINT_UDEC print_udec_1 ();  // open: num, start, CLK, RST, ASCII, Write_ASCII, end
  PRINT_DEC print_dec_1 (
    .num(in_1), .start(button_2_out), .CLK(CLK), .RST(CLR), .ASCII(ASCII), .Write_ASCII(Write_ASCII),
    .END(out_2));
  TTY #(.rows(32), .cols(60)) tty_1 (.data(ASCII), .clk(CLK), .we(Write_ASCII), .clr(CLR));
endmodule

module Print (
  input  in_1,
  input  in_2,
  input  in_3,
  input  [6:0] in_4,
  output WA,
  output [6:0] ASCII,
  output End
);

  wire _0__n_n__9, comparator_1_eq, comparator_1_lt, comparator_2_eq, comparator_2_lt, d_ff_1_q,
       demultiplexer_1_out0, demultiplexer_1_out1, or_1_out, or_2_out, or_4_out, T1, T2;
  wire [6:0] n_48, n_55;

  or or_1 (or_1_out, comparator_1_eq, comparator_1_lt);
  Comparator #(.width(7), .mode("unsigned")) comparator_1 (
    .a({7{1'b0}}), .b(in_4), .eq(comparator_1_eq), .lt(comparator_1_lt));  // open: gt
  Comparator #(.width(7), .mode("unsigned")) comparator_2 (
    .a(in_4), .b(7'b0001001), .eq(comparator_2_eq), .lt(comparator_2_lt));  // open: gt
  or or_2 (or_2_out, comparator_2_eq, comparator_2_lt);
  Adder #(.width(7)) adder_1 (.a(in_4), .b(7'b0110000), .out(n_48));  // open: cin, cout
  Demultiplexer #(.enable("false")) demultiplexer_1 (
    .out0(demultiplexer_1_out0), .out1(demultiplexer_1_out1), .in(d_ff_1_q), .sel(in_3));
  D_Flip_Flop d_ff_1 (.clk(in_1), .D(demultiplexer_1_out0), .Q(d_ff_1_q), .preset(in_2));  // open: Qn, en, reset
  and and_1 (_0__n_n__9, or_1_out, or_2_out);
  Adder #(.width(7)) adder_2 (.a(in_4), .b(7'b0110111), .out(n_55));  // open: cin, cout
  Demultiplexer #(.enable("false")) demultiplexer_2 (.out0(T2), .out1(T1), .in(demultiplexer_1_out1), .sel(_0__n_n__9));
  or or_3 (WA, T1, T2);
  Multiplexer #(.width(7), .enable("false")) multiplexer_1 (.in0(n_48), .in1(n_55), .out(ASCII), .sel(T2));
  or or_4 (or_4_out, T1, T2, End);
  D_Flip_Flop u_End (.clk(in_1), .D(or_4_out), .Q(End), .reset(in_2));  // open: Qn, preset, en

  // Other names for the same wires on the sheet: CLK = in_1; n[6:0] = in_4; RST = in_2; START = in_3
endmodule

module DataPath (
  input  in_1,
  input  in_2,
  input  in_3,
  input  in_4,
  input  in_5,
  input  in_6,
  input  [1:0] in_7,
  input  [31:0] in_8,
  input  [31:0] in_9,
  output offset_0,
  output out_11,
  output [31:0] out_12,
  output out_13,
  output [31:0] out_14
);

  wire [31:0] A, multiplexer_1_out, multiplexer_2_out, N, N_A_t, offset_1, offset_1_t;

  Multiplexer #(.width(32), .enable("false")) multiplexer_1 (
    .in0(in_8), .in1(N_A_t), .out(multiplexer_1_out), .sel(in_6));
  Register #(.width(32)) u_N (.D(multiplexer_1_out), .en(in_3), .Q(N), .clk(in_1), .clr(in_2));
  Comparator #(.width(32), .mode("unsigned")) comparator_1 (
    .a(N), .b({32{1'b0}}), .gt(out_11), .eq(out_13));  // open: lt
  Divider #(.width(32)) divider_1 (.a(N), .b(A), .out(N_A_t), .upper({32{1'b0}}), .rem(out_14));
  Register #(.width(32)) u_A (.D(in_9), .en(in_4), .Q(A), .clk(in_1), .clr(in_2));
  Comparator #(.width(32), .mode("unsigned")) comparator_2 (.a(out_12), .b({32{1'b0}}), .gt(offset_0));  // open: eq, lt
  Adder #(.width(32)) adder_1 (.a(out_12), .b(32'h1), .out(offset_1));  // open: cin, cout
  Subtractor #(.width(32)) subtractor_1 (.a(out_12), .b(32'h1), .out(offset_1_t));  // open: bin, bout
  Multiplexer #(.select(2), .width(32), .enable("false")) multiplexer_2 (
    .in0({32{1'b0}}), .in1(offset_1), .in2(offset_1_t), .out(multiplexer_2_out), .sel(in_7));  // open: in3
  Register #(.width(32)) Offset (.D(multiplexer_2_out), .en(in_5), .Q(out_12), .clk(in_1), .clr(in_2));

  // Other names for the same wires on the sheet: a_t[31:0] = in_9; CLK = in_1; LA = in_4; LN = in_3; Lof = in_5;
  //   N_0 = out_11; N__0 = out_13; N_A[31:0] = out_14; n_t[31:0] = in_8; offset[31:0] = out_12; RST = in_2; SN = in_6;
  //   Sof[1:0] = in_7
endmodule

module ControlUnit (
  input  in_1,
  input  in_2,
  input  in_3,
  input  State_Signals,
  input  in_5,
  input  EndPrint,
  input  [31:0] in_7,
  input  [31:0] in_8,
  input  in_9,
  input  [31:0] in_10,
  output END,
  output StartPrint,
  output LN,
  output LA,
  output Lof,
  output WriteMemory,
  output SN,
  output [1:0] Sof,
  output [23:0] ReadWriteAddress,
  output ResetPrint,
  output [6:0] ASCII_CODE,
  output [31:0] WriteContent
);

  wire d_ff_1_q, d_ff_2_q, d_ff_6_q, demultiplexer_1_out0, demultiplexer_2_out0, demultiplexer_3_out0,
       demultiplexer_4_out0, demultiplexer_5_out0, demultiplexer_5_out1, demultiplexer_6_out0,
       demultiplexer_6_out1, END0, END1, or_3_out, or_4_out, or_5_out, or_7_out, or_8_out, or_9_out,
       Print_2_q, Print_q, PrintSelector, ResetPrint0, ResetPrint1, StartPrint0;

  or or_1 (END, END0, END1);
  Demultiplexer #(.enable("false")) demultiplexer_1 (.out0(demultiplexer_1_out0), .out1(LA), .in(d_ff_1_q), .sel(in_3));
  D_Flip_Flop d_ff_1 (.clk(in_1), .D(demultiplexer_1_out0), .Q(d_ff_1_q), .preset(in_2));  // open: Qn, en, reset
  D_Flip_Flop d_ff_2 (.clk(in_1), .D(LA), .Q(d_ff_2_q), .reset(in_2));  // open: Qn, preset, en
  or or_2 (LN, LA, SN);
  Demultiplexer #(.enable("false")) demultiplexer_2 (
    .out0(demultiplexer_2_out0), .out1(ResetPrint0), .in(d_ff_2_q), .sel(State_Signals));
  Demultiplexer #(.enable("false")) demultiplexer_3 (
    .out0(demultiplexer_3_out0), .out1(WriteMemory), .in(or_3_out), .sel(in_5));
  or or_3 (or_3_out, demultiplexer_2_out0, d_ff_6_q);
  Demultiplexer #(.enable("false")) demultiplexer_4 (
    .out0(demultiplexer_4_out0), .out1(Sof[1]), .in(or_4_out), .sel(in_9));
  or or_4 (or_4_out, demultiplexer_3_out0, demultiplexer_6_out1);
  or or_5 (or_5_out, END1, demultiplexer_4_out0);
  D_Flip_Flop d_ff_3 (.clk(in_1), .D(ResetPrint0), .Q(StartPrint0), .reset(in_2));  // open: Qn, preset, en
  D_Flip_Flop d_ff_4 (.clk(in_1), .D(Sof[1]), .Q(ResetPrint1), .reset(in_2));  // open: Qn, preset, en
  D_Flip_Flop u_END (.clk(in_1), .D(or_5_out), .Q(END1), .reset(in_2));  // open: Qn, preset, en
  or or_6 (Lof, LA, SN, Sof[1]);
  D_Flip_Flop d_ff_5 (.clk(in_1), .D(WriteMemory), .Q(SN), .reset(in_2));  // open: Qn, preset, en
  D_Flip_Flop Print (.clk(in_1), .D(or_7_out), .Q(Print_q), .reset(in_2));  // open: Qn, preset, en
  or or_7 (or_7_out, demultiplexer_5_out0, StartPrint0);
  D_Flip_Flop d_ff_6 (.clk(in_1), .D(SN), .Q(d_ff_6_q), .reset(in_2));  // open: Qn, preset, en
  Demultiplexer #(.enable("false")) demultiplexer_5 (
    .out0(demultiplexer_5_out0), .out1(demultiplexer_5_out1), .in(Print_q), .sel(EndPrint));
  D_Flip_Flop d_ff_7 (.clk(in_1), .D(ResetPrint1), .Q(PrintSelector), .reset(in_2));  // open: Qn, preset, en
  D_Flip_Flop END_2 (.clk(in_1), .D(or_8_out), .Q(END0), .reset(in_2));  // open: Qn, preset, en
  or or_8 (or_8_out, END0, demultiplexer_5_out1);
  or or_9 (or_9_out, demultiplexer_6_out0, PrintSelector);
  Demultiplexer #(.enable("false")) demultiplexer_6 (
    .out0(demultiplexer_6_out0), .out1(demultiplexer_6_out1), .in(Print_2_q), .sel(EndPrint));
  D_Flip_Flop Print_2 (.clk(in_1), .D(or_9_out), .Q(Print_2_q), .reset(in_2));  // open: Qn, preset, en
  or or_10 (StartPrint, StartPrint0, PrintSelector);
  or or_11 (ResetPrint, ResetPrint0, ResetPrint1);
  Multiplexer #(.width(7), .enable("false")) multiplexer_1 (
    .in0({7{1'b0}}), .in1(in_10[6:0]), .out(ASCII_CODE), .sel(PrintSelector));

  assign ReadWriteAddress = in_7[23:0];
  assign Sof[0] = SN;
  assign WriteContent = in_8;

  // Other names for the same wires on the sheet: CLK = in_1; MemoryInput[31:0] = in_10; N_0 = in_5;
  //   N__0 = State_Signals; N_A[31:0] = in_8; offset[31:0] = in_7; offset_0 = in_9; RST = in_2; T2 = SN; T3 = Sof[1];
  //   START = in_3; StartPrint1 = PrintSelector; T1 = LA

  // Notes on the sheet:
  //   N=n
  //   A=a
  //   offset=0
  //   Data Path Control Signals
  //   Load To Memory
  //   offset=offset-1
  //   Tal vez haya que esperar a que la memoria cargue aqui
  //   offset=offset+1
  //   N=N/A
  //   Memory Control Signals
  //   Print Control Signals
  //   Input Control Signals
endmodule

module ASM (
  input  in_1,
  input  in_2,
  input  [31:0] Input_In,
  input  [31:0] Memory_In,
  output [23:0] Input_Address,
  output END,
  output Write,
  output Write_2,
  output [23:0] Address,
  output [6:0] ASCII,
  output [31:0] Memory_Out
);

  wire controlunit_1_la, controlunit_1_ln, controlunit_1_lof, controlunit_1_resetprint, controlunit_1_sn,
       controlunit_1_startprint, datapath_1_offset_0, datapath_1_out_11, datapath_1_out_13, or_1_out,
       print_1_end, Start;
  wire [1:0] controlunit_1_sof;
  wire [6:0] controlunit_1_ascii_code;
  wire [31:0] datapath_1_out_12, datapath_1_out_14, loader_1_out_4, loader_1_out_5;

  // Probe on loader_1_out_5
  // Probe on loader_1_out_4
  Loader loader_1 (
    .in_1(in_1), .in_2(in_2), .in_3(Input_In), .out_4(loader_1_out_4), .out_5(loader_1_out_5),
    .ReadAddress(Input_Address), .START_CU(Start));
  or or_1 (or_1_out, controlunit_1_resetprint, in_2);
  DataPath datapath_1 (
    .in_1(in_1), .in_2(in_2), .in_3(controlunit_1_ln), .in_4(controlunit_1_la), .in_5(controlunit_1_lof),
    .in_6(controlunit_1_sn), .in_7(controlunit_1_sof), .out_11(datapath_1_out_11),
    .out_13(datapath_1_out_13), .out_12(datapath_1_out_12), .out_14(datapath_1_out_14),
    .offset_0(datapath_1_offset_0), .in_8(loader_1_out_4), .in_9(loader_1_out_5));
  ControlUnit controlunit_1 (
    .in_1(in_1), .in_2(in_2), .in_3(Start), .END(END), .State_Signals(datapath_1_out_13),
    .in_5(datapath_1_out_11), .EndPrint(print_1_end), .in_7(datapath_1_out_12), .in_8(datapath_1_out_14),
    .in_9(datapath_1_offset_0), .in_10(Memory_In), .StartPrint(controlunit_1_startprint),
    .LN(controlunit_1_ln), .LA(controlunit_1_la), .Lof(controlunit_1_lof), .WriteMemory(Write),
    .SN(controlunit_1_sn), .Sof(controlunit_1_sof), .ReadWriteAddress(Address),
    .ResetPrint(controlunit_1_resetprint), .ASCII_CODE(controlunit_1_ascii_code), .WriteContent(Memory_Out));
  Print print_1 (
    .in_1(in_1), .in_2(or_1_out), .in_3(controlunit_1_startprint), .in_4(controlunit_1_ascii_code),
    .WA(Write_2), .ASCII(ASCII), .End(print_1_end));

  // Other names for the same wires on the sheet: CLK = in_1; RST = in_2
endmodule

module Loader (
  input  in_1,
  input  in_2,
  input  [31:0] in_3,
  output [31:0] out_4,
  output [31:0] out_5,
  output [23:0] ReadAddress,
  output START_CU
);

  wire La, Ln, or_1_out, WAIT_2_q;

  Register #(.width(32)) n (.D(in_3), .en(Ln), .Q(out_4), .clk(in_1), .clr(in_2));
  D_Flip_Flop IDLE (.clk(in_1), .D(1'b0), .Q(Ln), .preset(in_2));  // open: Qn, en, reset
  Register #(.width(32)) a (.D(in_3), .en(La), .Q(out_5), .clk(in_1), .clr(in_2));
  D_Flip_Flop WAIT (.clk(in_1), .D(Ln), .Q(La), .reset(in_2));  // open: Qn, preset, en
  D_Flip_Flop WAIT_2 (.clk(in_1), .D(La), .Q(WAIT_2_q), .reset(in_2));  // open: Qn, preset, en
  or or_1 (or_1_out, START_CU, WAIT_2_q);
  Multiplexer #(.width(24), .enable("false")) multiplexer_1 (
    .in0({24{1'b0}}), .in1(24'h1), .out(ReadAddress), .sel(La));
  D_Flip_Flop END (.clk(in_1), .D(or_1_out), .Q(START_CU), .reset(in_2));  // open: Qn, preset, en

  // Other names for the same wires on the sheet: a[31:0] = out_5; CLK = in_1; input[31:0] = in_3; n[31:0] = out_4;
  //   RST = in_2; Saddress = La

  // Notes on the sheet:
  //   Loader loads input
endmodule
