// Logisim project BigASM.circ as structural Verilog
module BOARD_BIG_ASM (
  output out_1
);

  wire button_1_out, CLK, CLR, d_ff_1_q, not_1_out, Write, Write_ASCII;
  wire [6:0] ASCII;
  wire [7:0] counter_1_q;
  wire [23:0] Dir_INPUT, Dir_MEMORY;
  wire [31:0] INPUT, MEMORY_IN, MEMORY_OUT;

  Button button_1 (.out(button_1_out));
  Clock clock_1 (.out(CLK));
  D_Flip_Flop d_ff_1 (.clk(CLK), .D(1'b1), .Q(d_ff_1_q), .reset(button_1_out));  // open: Qn, preset, en
  D_Flip_Flop d_ff_2 (.clk(CLK), .D(d_ff_1_q), .Qn(CLR), .reset(button_1_out));  // open: Q, preset, en
  BIG_ASM big_asm_1 (
    .DATA_INPUT(INPUT), .MEMORY_IN(MEMORY_OUT), .CLK(CLK), .CLR(CLR), .DIR_INPUT(Dir_INPUT),
    .MEMORY_OUT(MEMORY_IN), .DIR_MEMORY(Dir_MEMORY), .Write_OUTPUT(Write), .ASCII(ASCII),
    .Write_ASCII(Write_ASCII), .END(out_1));
  MEMORY memory_1 (.DIR(Dir_MEMORY), .DATA_IN(MEMORY_IN), .WRITE(Write), .CLK(CLK), .CLR(CLR), .DATA_OUT(MEMORY_OUT));
  INPUT input_1 (.DIR(Dir_INPUT), .CLK(CLK), .DATA_OUT(INPUT));
  Counter counter_1 (.load(1'b0), .count(not_1_out), .Q(counter_1_q), .clk(CLK), .clr(CLR));  // open: D, carry
  not not_1 (not_1_out, out_1);
  // Probe on counter_1_q
  TTY #(.rows(32), .cols(60)) tty_1 (.data(ASCII), .clk(CLK), .we(Write_ASCII), .clr(CLR));

  // Other names for the same wires on the sheet: END = out_1

  // Notes on the sheet:
  //   COUNTER
  //   BOARD
endmodule

module INPUT (
  input  [23:0] DIR,
  input  CLK,
  output [31:0] DATA_OUT
);

  RAM #(.addrWidth(24), .dataWidth(32)) ram_1 (.addr(DIR), .data(DATA_OUT), .clk(CLK), .ld(1'b1));  // open: sel, clr
endmodule

module MEMORY (
  input  [23:0] DIR,
  input  [31:0] DATA_IN,
  input  WRITE,
  input  CLK,
  input  CLR,
  output [31:0] DATA_OUT
);

  RAM #(.addrWidth(24), .dataWidth(32), .bus("separate")) ram_1 (
    .addr(DIR), .din(DATA_IN), .data(DATA_OUT), .str(WRITE), .clk(CLK), .clr(CLR));  // open: sel, ld
endmodule

module BIG_ASM (
  input  [31:0] DATA_INPUT,
  input  [31:0] MEMORY_IN,
  input  CLK,
  input  CLR,
  output [23:0] DIR_INPUT,
  output [31:0] MEMORY_OUT,
  output [23:0] DIR_MEMORY,
  output Write_OUTPUT,
  output [6:0] ASCII,
  output Write_ASCII,
  output END
);

  wire asm_1_out_8, asm_1_out_9, not_1_out, print_dec_1_end;
  wire [31:0] asm_1_num;

  not not_1 (not_1_out, CLR);
  ASM asm_1 (
    .in_1(CLK), .in_2(CLR), .in_3(not_1_out), .out_6(END), .in_4(DATA_INPUT), .in_5(print_dec_1_end),
    .out_8(asm_1_out_8), .out_9(asm_1_out_9), .NUM(asm_1_num));
  PRINT_DEC print_dec_1 (
    .num(asm_1_num), .start(asm_1_out_8), .CLK(CLK), .RST(asm_1_out_9), .ASCII(ASCII),
    .Write_ASCII(Write_ASCII), .END(print_dec_1_end));

  assign DIR_INPUT = {24{1'b0}};
endmodule

module PRINT_UDEC (
  input  [31:0] num,
  input  start,
  input  CLK,
  input  RST,
  output [6:0] ASCII,
  output Write_ASCII,
  output \end 
);

  wire _0_c, _0_n, demultiplexer_1_out0, demultiplexer_2_out0, demultiplexer_2_out1, demultiplexer_3_out0,
       demultiplexer_3_out1, IDLE_2_q, IDLE_3_q, IDLE_4_q, IDLE_q, Lc, Lc_0, Ln, Ln_0, or_1_out;
  wire [23:0] bit_extender_1_out;
  wire [31:0] c, c___1, c___1_t, divider_1_rem, memory_1_data_out, multiplexer_1_out, multiplexer_2_out,
       multiplexer_3_out, n, n___10, n___10___48;

  Multiplexer #(.width(32), .enable("false")) multiplexer_1 (
    .in0(num), .in1(n___10), .out(multiplexer_1_out), .sel(Lc_0));
  Divider #(.width(32)) divider_1 (.a(n), .b(32'ha), .out(n___10), .rem(divider_1_rem));  // open: upper
  Adder #(.width(32)) adder_1 (.a(divider_1_rem), .b(32'h30), .out(n___10___48));  // open: cin, cout
  or or_1 (or_1_out, demultiplexer_1_out0, \end );
  Register #(.width(32)) u_n (.D(multiplexer_1_out), .en(Ln), .Q(n), .clk(CLK), .clr(RST));
  D_Flip_Flop IDLE (.clk(CLK), .D(or_1_out), .Q(IDLE_q), .preset(RST));  // open: Qn, en, reset
  Demultiplexer #(.enable("false")) demultiplexer_1 (
    .out0(demultiplexer_1_out0), .out1(Ln_0), .in(IDLE_q), .sel(start));
  or or_2 (Write_ASCII, demultiplexer_3_out0, demultiplexer_2_out1);
  Multiplexer #(.width(32), .enable("false")) multiplexer_2 (
    .in0(c___1), .in1(c___1_t), .out(multiplexer_2_out), .sel(Write_ASCII));
  Adder #(.width(32)) adder_2 (.a(c), .b(32'h1), .out(c___1));  // open: cin, cout
  Subtractor #(.width(32)) subtractor_1 (.a(c), .b(32'h1), .out(c___1_t));  // open: bin, bout
  D_Flip_Flop IDLE_2 (.clk(CLK), .D(Ln_0), .Q(IDLE_2_q), .reset(RST));  // open: Qn, preset, en
  Register #(.width(32)) u_c (.D(multiplexer_2_out), .en(Lc), .Q(c), .clk(CLK), .clr(RST));
  or or_3 (Lc_0, IDLE_2_q, demultiplexer_3_out1);
  Multiplexer #(.width(32), .enable("false")) multiplexer_3 (
    .in0(c), .in1(c___1_t), .out(multiplexer_3_out), .sel(Write_ASCII));
  Comparator #(.width(32), .mode("unsigned")) comparator_1 (.a({32{1'b0}}), .b(n), .lt(_0_n));  // open: gt, eq
  Comparator #(.width(32), .mode("unsigned")) comparator_2 (.a({32{1'b0}}), .b(c), .lt(_0_c));  // open: gt, eq
  D_Flip_Flop IDLE_3 (.clk(CLK), .D(Write_ASCII), .Q(IDLE_3_q), .reset(RST));  // open: Qn, preset, en
  Demultiplexer #(.enable("false")) demultiplexer_2 (
    .out0(demultiplexer_2_out0), .out1(demultiplexer_2_out1), .in(IDLE_3_q), .sel(_0_c));
  Bit_Extender #(.in_width(32), .out_width(24)) bit_extender_1 (.in(multiplexer_3_out), .out(bit_extender_1_out));
  D_Flip_Flop IDLE_4 (.clk(CLK), .D(Lc_0), .Q(IDLE_4_q), .reset(RST));  // open: Qn, preset, en
  or or_4 (Lc, Lc_0, Write_ASCII);
  or or_5 (Ln, Ln_0, Lc_0);
  Demultiplexer #(.enable("false")) demultiplexer_3 (
    .out0(demultiplexer_3_out0), .out1(demultiplexer_3_out1), .in(IDLE_4_q), .sel(_0_n));
  D_Flip_Flop IDLE_5 (.clk(CLK), .D(demultiplexer_2_out0), .Q(\end ), .reset(RST));  // open: Qn, preset, en
  MEMORY memory_1 (
    .DIR(bit_extender_1_out), .DATA_IN(n___10___48), .WRITE(Lc_0), .CLK(CLK), .CLR(RST),
    .DATA_OUT(memory_1_data_out));
  Bit_Extender #(.in_width(32), .out_width(7)) bit_extender_2 (.in(memory_1_data_out), .out(ASCII));

  // Other names for the same wires on the sheet: Lc_1 = Write_ASCII; Sc = Write_ASCII; Ln_1 = Lc_0; Sn = Lc_0;
  //   Write = Lc_0
endmodule

module PRINT_DEC (
  input  [31:0] num,
  input  start,
  input  CLK,
  input  RST,
  output [6:0] ASCII,
  output Write_ASCII,
  output END
);

  wire demultiplexer_1_out0, demultiplexer_1_out1, demultiplexer_2_out0, demultiplexer_3_out0, end_t,
       IDLE_3_q, IDLE_q, or_1_out, or_2_out, or_3_out, S_ASCII, startUDEC, Write_ASCII_1;
  wire [6:0] ASCII_t;
  wire [31:0] multiplexer_1_out, negator_1_out;

  or or_1 (or_1_out, demultiplexer_1_out0, END);
  Negator #(.width(32)) negator_1 (.in(num), .out(negator_1_out));
  D_Flip_Flop IDLE (.clk(CLK), .D(or_1_out), .Q(IDLE_q), .preset(RST));  // open: Qn, en, reset
  Demultiplexer #(.enable("false")) demultiplexer_1 (
    .out0(demultiplexer_1_out0), .out1(demultiplexer_1_out1), .in(IDLE_q), .sel(start));
  Multiplexer #(.width(32), .enable("false")) multiplexer_1 (
    .in0(num), .in1(negator_1_out), .out(multiplexer_1_out), .sel(num[31]));
  Demultiplexer #(.enable("false")) demultiplexer_2 (
    .out0(demultiplexer_2_out0), .out1(S_ASCII), .in(demultiplexer_1_out1), .sel(num[31]));
  or or_2 (or_2_out, demultiplexer_2_out0, S_ASCII);
  D_Flip_Flop IDLE_2 (.clk(CLK), .D(or_2_out), .Q(startUDEC), .reset(RST));  // open: Qn, preset, en
  PRINT_UDEC print_udec_1 (
    .num(multiplexer_1_out), .start(startUDEC), .CLK(CLK), .RST(RST), .ASCII(ASCII_t),
    .Write_ASCII(Write_ASCII_1), .\end (end_t));
  D_Flip_Flop IDLE_3 (.clk(CLK), .D(or_3_out), .Q(IDLE_3_q), .reset(RST));  // open: Qn, preset, en
  or or_3 (or_3_out, startUDEC, demultiplexer_3_out0);
  Demultiplexer #(.enable("false")) demultiplexer_3 (
    .out0(demultiplexer_3_out0), .out1(END), .in(IDLE_3_q), .sel(end_t));
  Multiplexer #(.width(7), .enable("false")) multiplexer_2 (
    .in0(ASCII_t), .in1(7'b0101101), .out(ASCII), .sel(S_ASCII));
  or or_4 (Write_ASCII, S_ASCII, Write_ASCII_1);

  // Other names for the same wires on the sheet: sign = num[31]; Write_ASCII_0 = S_ASCII
endmodule

module TEST_PRINT (
  input  [31:0] in_1,
  output out_2
);

  wire button_1_out, button_2_out, CLK, CLR, d_ff_1_q, Write_ASCII;
  wire [6:0] ASCII;

  Button button_1 (.out(button_1_out));
  Clock clock_1 (.out(CLK));
  D_Flip_Flop d_ff_1 (.clk(CLK), .D(1'b1), .Q(d_ff_1_q), .reset(button_1_out));  // open: Qn, preset, en
  D_Flip_Flop d_ff_2 (.clk(CLK), .D(d_ff_1_q), .Qn(CLR), .reset(button_1_out));  // open: Q, preset, en
  Button button_2 (.out(button_2_out));
  PRINT_UDEC print_udec_1 ();  // open: num, start, CLK, RST, ASCII, Write_ASCII, end
  PRINT_DEC print_dec_1 (
    .num(in_1), .start(button_2_out), .CLK(CLK), .RST(CLR), .ASCII(ASCII), .Write_ASCII(Write_ASCII),
    .END(out_2));
  TTY #(.rows(32), .cols(60)) tty_1 (.data(ASCII), .clk(CLK), .we(Write_ASCII), .clr(CLR));
endmodule

module DataPath (
  input  in_1,
  input  in_2,
  input  [31:0] in_3,
  input  in_4,
  input  in_5,
  input  [1:0] in_6,
  input  in_7,
  output [31:0] out_8,
  output [31:0] out_9,
  output N_1,
  output i_i__N,
  output N_i__0,
  output N_2__0
);

  wire comparator_4_eq, comparator_4_lt;
  wire [31:0] i_2, i_i, multiplexer_1_out, multiplexer_2_out, N_2, N_2_t, N_i, N_i_t;

  Multiplexer #(.select(2), .width(32), .enable("false")) multiplexer_1 (
    .in0(in_3), .in1(N_2_t), .in2(N_i_t), .out(multiplexer_1_out), .sel(in_6));  // open: in3
  Divider #(.width(32)) divider_1 (.a(out_9), .b(32'h2), .out(N_2_t), .upper({32{1'b0}}), .rem(N_2));
  Comparator #(.width(32), .mode("unsigned")) comparator_1 (.a(out_9), .b(32'h1), .gt(N_1));  // open: eq, lt
  Comparator #(.width(32), .mode("unsigned")) comparator_2 (.a(N_2), .b({32{1'b0}}), .eq(N_2__0));  // open: gt, lt
  Register #(.width(32)) N (.D(multiplexer_1_out), .en(in_4), .Q(out_9), .clk(in_1), .clr(in_2));
  Divider #(.width(32)) divider_2 (.a(out_9), .b(out_8), .out(N_i_t), .upper({32{1'b0}}), .rem(N_i));
  Comparator #(.width(32), .mode("unsigned")) comparator_3 (.a(N_i), .b({32{1'b0}}), .eq(N_i__0));  // open: gt, lt
  Multiplexer #(.width(32), .enable("false")) multiplexer_2 (
    .in0(32'h3), .in1(i_2), .out(multiplexer_2_out), .sel(in_7));
  Register #(.width(32)) i (.D(multiplexer_2_out), .en(in_5), .Q(out_8), .clk(in_1), .clr(in_2));
  Multiplier #(.width(32)) multiplier_1 (.a(out_8), .b(out_8), .out(i_i));  // open: cin, cout
  Comparator #(.width(32), .mode("unsigned")) comparator_4 (
    .a(i_i), .b(out_9), .eq(comparator_4_eq), .lt(comparator_4_lt));  // open: gt
  Adder #(.width(32)) adder_1 (.a(out_8), .b(32'h2), .out(i_2));  // open: cin, cout
  or or_1 (i_i__N, comparator_4_eq, comparator_4_lt);

  // Other names for the same wires on the sheet: CLK = in_1; i[31:0] = out_8; Li = in_5; LN = in_4; N[31:0] = out_9;
  //   n_t[31:0] = in_3; RST = in_2; Si = in_7; SN[1:0] = in_6
endmodule

module ControlUnit (
  input  in_1,
  input  in_2,
  input  in_3,
  input  in_4,
  input  in_5,
  input  in_6,
  input  in_7,
  input  in_8,
  output out_9,
  output LN,
  output Li,
  output [1:0] SN,
  output Si,
  output StartPrint,
  output ResetPrint,
  output [1:0] SelectorPrint
);

  wire d_ff_1_q, d_ff_2_q, d_ff_3_q, demultiplexer_1_out0, demultiplexer_2_out0, demultiplexer_3_out0,
       demultiplexer_3_out1, demultiplexer_4_out0, demultiplexer_5_out0, demultiplexer_5_out1,
       demultiplexer_6_out0, demultiplexer_7_out0, demultiplexer_8_out0, demultiplexer_8_out1,
       demultiplexer_9_out0, demultiplexer_10_out0, demultiplexer_10_out1, IDLE_q, N_N_i_q, or_6_out,
       or_7_out, or_11_out, or_12_out, Print_2_q, Print_3_q, Print_q, RePr0, RePr1, RePr2, StPr0, T1;

  or or_1 (StartPrint, StPr0, SelectorPrint[1], SelectorPrint[0]);
  or or_2 (ResetPrint, RePr0, RePr2, RePr1);
  Demultiplexer #(.enable("false")) demultiplexer_1 (.out0(demultiplexer_1_out0), .out1(T1), .in(IDLE_q), .sel(in_3));
  D_Flip_Flop IDLE (.clk(in_1), .D(demultiplexer_1_out0), .Q(IDLE_q), .preset(in_2));  // open: Qn, en, reset
  or or_3 (LN, T1, SN[0], SN[1]);
  Demultiplexer #(.enable("false")) demultiplexer_2 (
    .out0(demultiplexer_2_out0), .out1(RePr0), .in(d_ff_1_q), .sel(in_4));
  D_Flip_Flop d_ff_1 (.clk(in_1), .D(T1), .Q(d_ff_1_q), .reset(in_2));  // open: Qn, preset, en
  or or_4 (StPr0, RePr0, demultiplexer_3_out0);
  or or_5 (Li, T1, Si);
  D_Flip_Flop Print (.clk(in_1), .D(StPr0), .Q(Print_q), .reset(in_2));  // open: Qn, preset, en
  Demultiplexer #(.enable("false")) demultiplexer_3 (
    .out0(demultiplexer_3_out0), .out1(demultiplexer_3_out1), .in(Print_q), .sel(in_8));
  Demultiplexer #(.enable("false")) demultiplexer_4 (
    .out0(demultiplexer_4_out0), .out1(SN[0]), .in(or_6_out), .sel(in_4));
  or or_6 (or_6_out, demultiplexer_2_out0, demultiplexer_3_out1, d_ff_2_q);
  D_Flip_Flop d_ff_2 (.clk(in_1), .D(SN[0]), .Q(d_ff_2_q), .reset(in_2));  // open: Qn, preset, en
  Demultiplexer #(.enable("false")) demultiplexer_5 (
    .out0(demultiplexer_5_out0), .out1(demultiplexer_5_out1), .in(or_7_out), .sel(in_6));
  or or_7 (or_7_out, demultiplexer_4_out0, d_ff_3_q);
  Demultiplexer #(.enable("false")) demultiplexer_6 (
    .out0(demultiplexer_6_out0), .out1(RePr1), .in(demultiplexer_5_out1), .sel(in_5));
  Demultiplexer #(.enable("false")) demultiplexer_7 (
    .out0(demultiplexer_7_out0), .out1(RePr2), .in(demultiplexer_5_out0), .sel(in_7));
  or or_8 (Si, demultiplexer_6_out0, demultiplexer_9_out0);
  or or_9 (SelectorPrint[0], demultiplexer_8_out0, RePr1);
  D_Flip_Flop d_ff_3 (.clk(in_1), .D(Si), .Q(d_ff_3_q), .reset(in_2));  // open: Qn, preset, en
  Demultiplexer #(.enable("false")) demultiplexer_8 (
    .out0(demultiplexer_8_out0), .out1(demultiplexer_8_out1), .in(Print_2_q), .sel(in_8));
  D_Flip_Flop Print_2 (.clk(in_1), .D(SelectorPrint[0]), .Q(Print_2_q), .reset(in_2));  // open: Qn, preset, en
  D_Flip_Flop Print_3 (.clk(in_1), .D(SelectorPrint[1]), .Q(Print_3_q), .reset(in_2));  // open: Qn, preset, en
  or or_10 (SelectorPrint[1], demultiplexer_10_out0, RePr2);
  Demultiplexer #(.enable("false")) demultiplexer_9 (
    .out0(demultiplexer_9_out0), .out1(SN[1]), .in(or_11_out), .sel(in_5));
  or or_11 (or_11_out, N_N_i_q, demultiplexer_8_out1);
  or or_12 (or_12_out, out_9, demultiplexer_7_out0, demultiplexer_10_out1);
  Demultiplexer #(.enable("false")) demultiplexer_10 (
    .out0(demultiplexer_10_out0), .out1(demultiplexer_10_out1), .in(Print_3_q), .sel(in_8));
  D_Flip_Flop d_ff_4 (.clk(in_1), .D(or_12_out), .Q(out_9), .reset(in_2));  // open: Qn, preset, en
  D_Flip_Flop N_N_i (.clk(in_1), .D(SN[1]), .Q(N_N_i_q), .reset(in_2));  // open: Qn, preset, en

  // Other names for the same wires on the sheet: CLK = in_1; END = out_9; EndPrint = in_8; i_i__N = in_6; N_1 = in_7;
  //   N_2__0 = in_4; N_i__0 = in_5; RST = in_2; SePr0 = SelectorPrint[0]; StPr1 = SelectorPrint[0];
  //   SePr1 = SelectorPrint[1]; StPr2 = SelectorPrint[1]; T2 = SN[0]; T4 = SN[1]; START = in_3; T3 = Si

  // Notes on the sheet:
  //   Senales de Control
  //   N=n
  //   i=3
  //   Senales de Estado
  //   N=N/2
  //   i=i+2
endmodule

module ASM (
  input  in_1,
  input  in_2,
  input  in_3,
  input  [31:0] in_4,
  input  in_5,
  output out_6,
  output [31:0] NUM,
  output out_8,
  output out_9
);

  wire controlunit_1_li, controlunit_1_ln, controlunit_1_si, datapath_1_i_i__n, datapath_1_n_1,
       datapath_1_n_2__0, datapath_1_n_i__0;
  wire [1:0] controlunit_1_selectorprint, controlunit_1_sn;
  wire [31:0] datapath_1_out_8, datapath_1_out_9;

  ControlUnit controlunit_1 (
    .in_1(in_1), .in_2(in_2), .in_3(in_3), .in_4(datapath_1_n_2__0), .in_5(datapath_1_n_i__0),
    .in_6(datapath_1_i_i__n), .in_7(datapath_1_n_1), .in_8(in_5), .out_9(out_6), .LN(controlunit_1_ln),
    .Li(controlunit_1_li), .SN(controlunit_1_sn), .Si(controlunit_1_si), .StartPrint(out_8),
    .ResetPrint(out_9), .SelectorPrint(controlunit_1_selectorprint));
  DataPath datapath_1 (
    .in_1(in_1), .in_2(in_2), .in_4(controlunit_1_ln), .in_5(controlunit_1_li), .in_6(controlunit_1_sn),
    .in_7(controlunit_1_si), .N_1(datapath_1_n_1), .i_i__N(datapath_1_i_i__n), .N_i__0(datapath_1_n_i__0),
    .N_2__0(datapath_1_n_2__0), .in_3(in_4), .out_8(datapath_1_out_8), .out_9(datapath_1_out_9));
  Multiplexer #(.select(2), .width(32), .enable("false")) multiplexer_1 (
    .in0(32'h2), .in1(datapath_1_out_8), .in2(datapath_1_out_9), .out(NUM), .sel(controlunit_1_selectorprint));  // open: in3

  // Other names for the same wires on the sheet: CLK = in_1; RST = in_2; START = in_3
endmodule
