// Logisim project BigASM.circ as structural Verilog
module BOARD_BIG_ASM (
  output out_1
);

  wire button_1_out, CLK, CLR, d_ff_1_q, not_1_out, Write, Write_ASCII;
  wire [6:0] ASCII;
  wire [7:0] counter_1_q;
  wire [23:0] Dir_INPUT, Dir_MEMORY;
  wire [31:0] INPUT, MEMORY_IN, MEMORY_OUT;

  Button button_1 (.out(button_1_out));
  Clock clock_1 (.out(CLK));
  D_Flip_Flop d_ff_1 (.clk(CLK), .D(1'b1), .Q(d_ff_1_q), .reset(button_1_out));  // open: Qn, preset, en
  D_Flip_Flop d_ff_2 (.clk(CLK), .D(d_ff_1_q), .Qn(CLR), .reset(button_1_out));  // open: Q, preset, en
  BIG_ASM big_asm_1 (
    .DATA_INPUT(INPUT), .MEMORY_IN(MEMORY_OUT), .CLK(CLK), .CLR(CLR), .DIR_INPUT(Dir_INPUT),
    .MEMORY_OUT(MEMORY_IN), .DIR_MEMORY(Dir_MEMORY), .Write_OUTPUT(Write), .ASCII(ASCII),
    .Write_ASCII(Write_ASCII), .END(out_1));
  MEMORY memory_1 (.DIR(Dir_MEMORY), .DATA_IN(MEMORY_IN), .WRITE(Write), .CLK(CLK), .CLR(CLR), .DATA_OUT(MEMORY_OUT));
  INPUT input_1 (.DIR(Dir_INPUT), .CLK(CLK), .DATA_OUT(INPUT));
  Counter counter_1 (.load(1'b0), .count(not_1_out), .Q(counter_1_q), .clk(CLK), .clr(CLR));  // open: D, carry
  not not_1 (not_1_out, out_1);
  // Probe on counter_1_q
  TTY #(.rows(32), .cols(60)) tty_1 (.data(ASCII), .clk(CLK), .we(Write_ASCII), .clr(CLR));

  // Other names for the same wires on the sheet: END = out_1

  // Notes on the sheet:
  //   COUNTER
  //   BOARD
endmodule

module INPUT (
  input  [23:0] DIR,
  input  CLK,
  output [31:0] DATA_OUT
);

  RAM #(.addrWidth(24), .dataWidth(32)) ram_1 (.addr(DIR), .data(DATA_OUT), .clk(CLK), .ld(1'b1));  // open: sel, clr
endmodule

module MEMORY (
  input  [23:0] DIR,
  input  [31:0] DATA_IN,
  input  WRITE,
  input  CLK,
  input  CLR,
  output [31:0] DATA_OUT
);

  RAM #(.addrWidth(24), .dataWidth(32), .bus("separate")) ram_1 (
    .addr(DIR), .din(DATA_IN), .data(DATA_OUT), .str(WRITE), .clk(CLK), .clr(CLR));  // open: sel, ld
endmodule

module BIG_ASM (
  input  [31:0] DATA_INPUT,
  input  [31:0] MEMORY_IN,
  input  CLK,
  input  CLR,
  output [23:0] DIR_INPUT,
  output [31:0] MEMORY_OUT,
  output [23:0] DIR_MEMORY,
  output Write_OUTPUT,
  output [6:0] ASCII,
  output Write_ASCII,
  output END
);

  wire and_1_out, fibasm_1_out_5, not_1_out, not_2_out, or_1_out, print_dec_1_end;
  wire [31:0] fibasm_1_out_6;

  not not_1 (not_1_out, CLR);
  and and_1 (and_1_out, fibasm_1_out_5, not_2_out);
  not not_2 (not_2_out, END);
  FibASM fibasm_1 (
    .in_1(CLK), .in_2(CLR), .in_3(not_1_out), .out_5(fibasm_1_out_5), .out_6(fibasm_1_out_6),
    .in_4(DATA_INPUT));
  PRINT_DEC print_dec_1 (
    .num(fibasm_1_out_6), .start(and_1_out), .CLK(CLK), .RST(CLR), .ASCII(ASCII), .Write_ASCII(Write_ASCII),
    .END(print_dec_1_end));
  or or_1 (or_1_out, END, print_dec_1_end);
  D_Flip_Flop d_ff_1 (.clk(CLK), .D(or_1_out), .Q(END), .reset(CLR));  // open: Qn, preset, en

  assign DIR_INPUT = {24{1'b0}};

  // Other names for the same wires on the sheet: Ith_Fib[31:0] = DATA_INPUT; RST = CLR
endmodule

module PRINT_UDEC (
  input  [31:0] num,
  input  start,
  input  CLK,
  input  RST,
  output [6:0] ASCII,
  output Write_ASCII,
  output \end 
);

  wire _0_c, _0_n, demultiplexer_1_out0, demultiplexer_2_out0, demultiplexer_2_out1, demultiplexer_3_out0,
       demultiplexer_3_out1, IDLE_2_q, IDLE_3_q, IDLE_4_q, IDLE_q, Lc, Lc_0, Ln, Ln_0, or_1_out;
  wire [23:0] bit_extender_1_out;
  wire [31:0] c, c___1, c___1_t, divider_1_rem, memory_1_data_out, multiplexer_1_out, multiplexer_2_out,
       multiplexer_3_out, n, n___10, n___10___48;

  Multiplexer #(.width(32), .enable("false")) multiplexer_1 (
    .in0(num), .in1(n___10), .out(multiplexer_1_out), .sel(Lc_0));
  Divider #(.width(32)) divider_1 (.a(n), .b(32'ha), .out(n___10), .rem(divider_1_rem));  // open: upper
  Adder #(.width(32)) adder_1 (.a(divider_1_rem), .b(32'h30), .out(n___10___48));  // open: cin, cout
  or or_1 (or_1_out, demultiplexer_1_out0, \end );
  Register #(.width(32)) u_n (.D(multiplexer_1_out), .en(Ln), .Q(n), .clk(CLK), .clr(RST));
  D_Flip_Flop IDLE (.clk(CLK), .D(or_1_out), .Q(IDLE_q), .preset(RST));  // open: Qn, en, reset
  Demultiplexer #(.enable("false")) demultiplexer_1 (
    .out0(demultiplexer_1_out0), .out1(Ln_0), .in(IDLE_q), .sel(start));
  or or_2 (Write_ASCII, demultiplexer_3_out0, demultiplexer_2_out1);
  Multiplexer #(.width(32), .enable("false")) multiplexer_2 (
    .in0(c___1), .in1(c___1_t), .out(multiplexer_2_out), .sel(Write_ASCII));
  Adder #(.width(32)) adder_2 (.a(c), .b(32'h1), .out(c___1));  // open: cin, cout
  Subtractor #(.width(32)) subtractor_1 (.a(c), .b(32'h1), .out(c___1_t));  // open: bin, bout
  D_Flip_Flop IDLE_2 (.clk(CLK), .D(Ln_0), .Q(IDLE_2_q), .reset(RST));  // open: Qn, preset, en
  Register #(.width(32)) u_c (.D(multiplexer_2_out), .en(Lc), .Q(c), .clk(CLK), .clr(RST));
  or or_3 (Lc_0, IDLE_2_q, demultiplexer_3_out1);
  Multiplexer #(.width(32), .enable("false")) multiplexer_3 (
    .in0(c), .in1(c___1_t), .out(multiplexer_3_out), .sel(Write_ASCII));
  Comparator #(.width(32), .mode("unsigned")) comparator_1 (.a({32{1'b0}}), .b(n), .lt(_0_n));  // open: gt, eq
  Comparator #(.width(32), .mode("unsigned")) comparator_2 (.a({32{1'b0}}), .b(c), .lt(_0_c));  // open: gt, eq
  D_Flip_Flop IDLE_3 (.clk(CLK), .D(Write_ASCII), .Q(IDLE_3_q), .reset(RST));  // open: Qn, preset, en
  Demultiplexer #(.enable("false")) demultiplexer_2 (
    .out0(demultiplexer_2_out0), .out1(demultiplexer_2_out1), .in(IDLE_3_q), .sel(_0_c));
  Bit_Extender #(.in_width(32), .out_width(24)) bit_extender_1 (.in(multiplexer_3_out), .out(bit_extender_1_out));
  D_Flip_Flop IDLE_4 (.clk(CLK), .D(Lc_0), .Q(IDLE_4_q), .reset(RST));  // open: Qn, preset, en
  or or_4 (Lc, Lc_0, Write_ASCII);
  or or_5 (Ln, Ln_0, Lc_0);
  Demultiplexer #(.enable("false")) demultiplexer_3 (
    .out0(demultiplexer_3_out0), .out1(demultiplexer_3_out1), .in(IDLE_4_q), .sel(_0_n));
  D_Flip_Flop IDLE_5 (.clk(CLK), .D(demultiplexer_2_out0), .Q(\end ), .reset(RST));  // open: Qn, preset, en
  MEMORY memory_1 (
    .DIR(bit_extender_1_out), .DATA_IN(n___10___48), .WRITE(Lc_0), .CLK(CLK), .CLR(RST),
    .DATA_OUT(memory_1_data_out));
  Bit_Extender #(.in_width(32), .out_width(7)) bit_extender_2 (.in(memory_1_data_out), .out(ASCII));

  // Other names for the same wires on the sheet: Lc_1 = Write_ASCII; Sc = Write_ASCII; Ln_1 = Lc_0; Sn = Lc_0;
  //   Write = Lc_0
endmodule

module PRINT_DEC (
  input  [31:0] num,
  input  start,
  input  CLK,
  input  RST,
  output [6:0] ASCII,
  output Write_ASCII,
  output END
);

  wire demultiplexer_1_out0, demultiplexer_1_out1, demultiplexer_2_out0, demultiplexer_3_out0, end_t,
       IDLE_3_q, IDLE_q, or_1_out, or_2_out, or_3_out, S_ASCII, startUDEC, Write_ASCII_1;
  wire [6:0] ASCII_t;
  wire [31:0] multiplexer_1_out, negator_1_out;

  or or_1 (or_1_out, demultiplexer_1_out0, END);
  Negator #(.width(32)) negator_1 (.in(num), .out(negator_1_out));
  D_Flip_Flop IDLE (.clk(CLK), .D(or_1_out), .Q(IDLE_q), .preset(RST));  // open: Qn, en, reset
  Demultiplexer #(.enable("false")) demultiplexer_1 (
    .out0(demultiplexer_1_out0), .out1(demultiplexer_1_out1), .in(IDLE_q), .sel(start));
  Multiplexer #(.width(32), .enable("false")) multiplexer_1 (
    .in0(num), .in1(negator_1_out), .out(multiplexer_1_out), .sel(num[31]));
  Demultiplexer #(.enable("false")) demultiplexer_2 (
    .out0(demultiplexer_2_out0), .out1(S_ASCII), .in(demultiplexer_1_out1), .sel(num[31]));
  or or_2 (or_2_out, demultiplexer_2_out0, S_ASCII);
  D_Flip_Flop IDLE_2 (.clk(CLK), .D(or_2_out), .Q(startUDEC), .reset(RST));  // open: Qn, preset, en
  PRINT_UDEC print_udec_1 (
    .num(multiplexer_1_out), .start(startUDEC), .CLK(CLK), .RST(RST), .ASCII(ASCII_t),
    .Write_ASCII(Write_ASCII_1), .\end (end_t));
  D_Flip_Flop IDLE_3 (.clk(CLK), .D(or_3_out), .Q(IDLE_3_q), .reset(RST));  // open: Qn, preset, en
  or or_3 (or_3_out, startUDEC, demultiplexer_3_out0);
  Demultiplexer #(.enable("false")) demultiplexer_3 (
    .out0(demultiplexer_3_out0), .out1(END), .in(IDLE_3_q), .sel(end_t));
  Multiplexer #(.width(7), .enable("false")) multiplexer_2 (
    .in0(ASCII_t), .in1(7'b0101101), .out(ASCII), .sel(S_ASCII));
  or or_4 (Write_ASCII, S_ASCII, Write_ASCII_1);

  // Other names for the same wires on the sheet: sign = num[31]; Write_ASCII_0 = S_ASCII
endmodule

module TEST_PRINT (
  input  [31:0] in_1,
  output out_2
);

  wire button_1_out, button_2_out, CLK, CLR, d_ff_1_q, Write_ASCII;
  wire [6:0] ASCII;

  Button button_1 (.out(button_1_out));
  Clock clock_1 (.out(CLK));
  D_Flip_Flop d_ff_1 (.clk(CLK), .D(1'b1), .Q(d_ff_1_q), .reset(button_1_out));  // open: Qn, preset, en
  D_Flip_Flop d_ff_2 (.clk(CLK), .D(d_ff_1_q), .Qn(CLR), .reset(button_1_out));  // open: Q, preset, en
  Button button_2 (.out(button_2_out));
  PRINT_UDEC print_udec_1 ();  // open: num, start, CLK, RST, ASCII, Write_ASCII, end
  PRINT_DEC print_dec_1 (
    .num(in_1), .start(button_2_out), .CLK(CLK), .RST(CLR), .ASCII(ASCII), .Write_ASCII(Write_ASCII),
    .END(out_2));
  TTY #(.rows(32), .cols(60)) tty_1 (.data(ASCII), .clk(CLK), .we(Write_ASCII), .clr(CLR));
endmodule

module DataPath (
  input  in_1,
  input  in_2,
  input  Sa,
  input  Sb,
  input  Si,
  input  [31:0] I,
  input  La,
  input  Lb,
  input  Lc,
  input  Li,
  output [31:0] out_11,
  output out_12
);

  wire [31:0] b, b_c, c, i_1, i_t, multiplexer_1_out, multiplexer_2_out, multiplexer_3_out;

  Multiplexer #(.width(32), .enable("false")) multiplexer_1 (
    .in0({32{1'b0}}), .in1(b), .out(multiplexer_1_out), .sel(Sa));
  Register #(.width(32)) a (.D(multiplexer_1_out), .en(La), .Q(out_11), .clk(in_1), .clr(in_2));
  Multiplexer #(.width(32), .enable("false")) multiplexer_2 (.in0(32'h1), .in1(b_c), .out(multiplexer_2_out), .sel(Sb));
  Register #(.width(32)) u_b (.D(multiplexer_2_out), .en(Lb), .Q(b), .clk(in_1), .clr(in_2));
  Adder #(.width(32)) adder_1 (.a(b), .b(c), .out(b_c));  // open: cin, cout
  Register #(.width(32)) u_c (.D(out_11), .en(Lc), .Q(c), .clk(in_1), .clr(in_2));
  Multiplexer #(.width(32), .enable("false")) multiplexer_3 (.in0(I), .in1(i_1), .out(multiplexer_3_out), .sel(Si));
  Register #(.width(32)) u_i (.D(multiplexer_3_out), .en(Li), .Q(i_t), .clk(in_1), .clr(in_2));
  Subtractor #(.width(32)) subtractor_1 (.a(i_t), .b(32'h1), .out(i_1));  // open: bin, bout
  Comparator #(.width(32), .mode("unsigned")) comparator_1 (.a(i_t), .b({32{1'b0}}), .gt(out_12));  // open: eq, lt

  // Other names for the same wires on the sheet: a[31:0] = out_11; CLK = in_1; i_0 = out_12; RST = in_2
endmodule

module ControlUnit (
  input  in_1,
  input  in_2,
  input  in_3,
  input  in_4,
  output END,
  output La,
  output Lb,
  output Lc,
  output Li,
  output Sa,
  output Sb,
  output Si
);

  wire d_ff_1_q, d_ff_4_q, demultiplexer_1_out0, demultiplexer_2_out0, IDLE_q, or_3_out, or_5_out, T1;

  or or_1 (La, T1, Sa);
  Demultiplexer #(.enable("false")) demultiplexer_1 (.out0(demultiplexer_1_out0), .out1(T1), .in(IDLE_q), .sel(in_3));
  D_Flip_Flop IDLE (.clk(in_1), .D(demultiplexer_1_out0), .Q(IDLE_q), .preset(in_2));  // open: Qn, en, reset
  or or_2 (Lb, T1, Sb);
  D_Flip_Flop d_ff_1 (.clk(in_1), .D(T1), .Q(d_ff_1_q), .reset(in_2));  // open: Qn, preset, en
  Demultiplexer #(.enable("false")) demultiplexer_2 (.out0(demultiplexer_2_out0), .out1(Lc), .in(or_3_out), .sel(in_4));
  or or_3 (or_3_out, d_ff_1_q, d_ff_4_q);
  or or_4 (Li, T1, Lc);
  or or_5 (or_5_out, END, demultiplexer_2_out0);
  D_Flip_Flop d_ff_2 (.clk(in_1), .D(Lc), .Q(Sa), .reset(in_2));  // open: Qn, preset, en
  D_Flip_Flop u_End (.clk(in_1), .D(or_5_out), .Q(END), .reset(in_2));  // open: Qn, preset, en
  D_Flip_Flop d_ff_3 (.clk(in_1), .D(Sa), .Q(Sb), .reset(in_2));  // open: Qn, preset, en
  D_Flip_Flop d_ff_4 (.clk(in_1), .D(Sb), .Q(d_ff_4_q), .reset(in_2));  // open: Qn, preset, en

  assign Si = Lc;

  // Other names for the same wires on the sheet: CLK = in_1; i_0 = in_4; RST = in_2; START = in_3; T2 = Lc; T3 = Sa;
  //   T4 = Sb

  // Notes on the sheet:
  //   Senales de control
  //   a=0
  //   b=1
  //   i=I
  //   i>0
  //   c=a
  //   i=i-1
  //   a=b
  //   b=b+c
endmodule

module FibASM (
  input  in_1,
  input  in_2,
  input  in_3,
  input  [31:0] in_4,
  output out_5,
  output [31:0] out_6
);

  wire controlunit_1_la, controlunit_1_lb, controlunit_1_lc, controlunit_1_li, controlunit_1_sa,
       controlunit_1_sb, controlunit_1_si, datapath_1_out_12;

  ControlUnit controlunit_1 (
    .in_1(in_1), .in_2(in_2), .in_3(in_3), .in_4(datapath_1_out_12), .La(controlunit_1_la),
    .Lb(controlunit_1_lb), .Lc(controlunit_1_lc), .Li(controlunit_1_li), .Sa(controlunit_1_sa),
    .Sb(controlunit_1_sb), .Si(controlunit_1_si), .END(out_5));
  // Probe on out_6
  DataPath datapath_1 (
    .in_1(in_1), .in_2(in_2), .Sa(controlunit_1_sa), .Sb(controlunit_1_sb), .Si(controlunit_1_si), .I(in_4),
    .La(controlunit_1_la), .Lb(controlunit_1_lb), .Lc(controlunit_1_lc), .Li(controlunit_1_li),
    .out_11(out_6), .out_12(datapath_1_out_12));

  // Other names for the same wires on the sheet: a[31:0] = out_6; CLK = in_1; END = out_5; I[31:0] = in_4; RST = in_2;
  //   START = in_3
endmodule
