// Logisim project BigASM.circ as structural Verilog
module BOARD_BIG_ASM (
  output out_1
);

  wire button_1_out, CLK, CLR, d_ff_1_q, not_1_out, Write, Write_ASCII;
  wire [6:0] ASCII;
  wire [7:0] counter_1_q;
  wire [23:0] Dir_INPUT, Dir_MEMORY;
  wire [31:0] INPUT, MEMORY_IN, MEMORY_OUT;

  Button button_1 (.out(button_1_out));
  Clock clock_1 (.out(CLK));
  D_Flip_Flop d_ff_1 (.clk(CLK), .D(1'b1), .Q(d_ff_1_q), .reset(button_1_out));  // open: Qn, preset, en
  D_Flip_Flop d_ff_2 (.clk(CLK), .D(d_ff_1_q), .Qn(CLR), .reset(button_1_out));  // open: Q, preset, en
  BIG_ASM big_asm_1 (
    .DATA_INPUT(INPUT), .MEMORY_IN(MEMORY_OUT), .CLK(CLK), .CLR(CLR), .DIR_INPUT(Dir_INPUT),
    .MEMORY_OUT(MEMORY_IN), .DIR_MEMORY(Dir_MEMORY), .Write_OUTPUT(Write), .ASCII(ASCII),
    .Write_ASCII(Write_ASCII), .END(out_1));
  MEMORY memory_1 (.DIR(Dir_MEMORY), .DATA_IN(MEMORY_IN), .WRITE(Write), .CLK(CLK), .CLR(CLR), .DATA_OUT(MEMORY_OUT));
  INPUT input_1 (.DIR(Dir_INPUT), .CLK(CLK), .DATA_OUT(INPUT));
  Counter counter_1 (.load(1'b0), .count(not_1_out), .Q(counter_1_q), .clk(CLK), .clr(CLR));  // open: D, carry
  not not_1 (not_1_out, out_1);
  // Probe on counter_1_q
  TTY #(.rows(32), .cols(60)) tty_1 (.data(ASCII), .clk(CLK), .we(Write_ASCII), .clr(CLR));

  // Other names for the same wires on the sheet: END = out_1

  // Notes on the sheet:
  //   COUNTER
  //   BOARD
endmodule

module INPUT (
  input  [23:0] DIR,
  input  CLK,
  output [31:0] DATA_OUT
);

  RAM #(.addrWidth(24), .dataWidth(32)) ram_1 (.addr(DIR), .data(DATA_OUT), .clk(CLK), .ld(1'b1));  // open: sel, clr
endmodule

module MEMORY (
  input  [23:0] DIR,
  input  [31:0] DATA_IN,
  input  WRITE,
  input  CLK,
  input  CLR,
  output [31:0] DATA_OUT
);

  wire not_1_out;

  not not_1 (not_1_out, WRITE);
  RAM #(.addrWidth(24), .dataWidth(32), .bus("separate")) ram_1 (
    .addr(DIR), .din(DATA_IN), .data(DATA_OUT), .clk(CLK), .ld(not_1_out), .clr(CLR));  // open: str, sel
endmodule

module BIG_ASM (
  input  [31:0] DATA_INPUT,
  input  [31:0] MEMORY_IN,
  input  CLK,
  input  CLR,
  output [23:0] DIR_INPUT,
  output [31:0] MEMORY_OUT,
  output [23:0] DIR_MEMORY,
  output Write_OUTPUT,
  output [6:0] ASCII,
  output Write_ASCII,
  output END
);

  ASM asm_1 (
    .in_1(CLK), .in_2(CLR), .Data_Input(DATA_INPUT), .out_6(ASCII), .out_7(Write_ASCII), .out_4(DIR_INPUT),
    .out_5(END));
endmodule

module PRINT_UDEC (
  input  [31:0] num,
  input  start,
  input  CLK,
  input  RST,
  output [6:0] ASCII,
  output Write_ASCII,
  output \end 
);

  wire _0_c, _0_n, demultiplexer_1_out0, demultiplexer_2_out0, demultiplexer_2_out1, demultiplexer_3_out0,
       demultiplexer_3_out1, IDLE_2_q, IDLE_3_q, IDLE_4_q, IDLE_q, Lc, Lc_0, Ln, Ln_0, or_1_out;
  wire [23:0] bit_extender_1_out;
  wire [31:0] c, c___1, c___1_t, divider_1_rem, memory_1_data_out, multiplexer_1_out, multiplexer_2_out,
       multiplexer_3_out, n, n___10, n___10___48;

  Multiplexer #(.width(32), .enable("false")) multiplexer_1 (
    .in0(num), .in1(n___10), .out(multiplexer_1_out), .sel(Lc_0));
  Divider #(.width(32)) divider_1 (.a(n), .b(32'ha), .out(n___10), .rem(divider_1_rem));  // open: upper
  Adder #(.width(32)) adder_1 (.a(divider_1_rem), .b(32'h30), .out(n___10___48));  // open: cin, cout
  or or_1 (or_1_out, demultiplexer_1_out0, \end );
  Register #(.width(32)) u_n (.D(multiplexer_1_out), .en(Ln), .Q(n), .clk(CLK), .clr(RST));
  D_Flip_Flop IDLE (.clk(CLK), .D(or_1_out), .Q(IDLE_q), .preset(RST));  // open: Qn, en, reset
  Demultiplexer #(.enable("false")) demultiplexer_1 (
    .out0(demultiplexer_1_out0), .out1(Ln_0), .in(IDLE_q), .sel(start));
  or or_2 (Write_ASCII, demultiplexer_3_out0, demultiplexer_2_out1);
  Multiplexer #(.width(32), .enable("false")) multiplexer_2 (
    .in0(c___1), .in1(c___1_t), .out(multiplexer_2_out), .sel(Write_ASCII));
  Adder #(.width(32)) adder_2 (.a(c), .b(32'h1), .out(c___1));  // open: cin, cout
  Subtractor #(.width(32)) subtractor_1 (.a(c), .b(32'h1), .out(c___1_t));  // open: bin, bout
  D_Flip_Flop IDLE_2 (.clk(CLK), .D(Ln_0), .Q(IDLE_2_q), .reset(RST));  // open: Qn, preset, en
  Register #(.width(32)) u_c (.D(multiplexer_2_out), .en(Lc), .Q(c), .clk(CLK), .clr(RST));
  or or_3 (Lc_0, IDLE_2_q, demultiplexer_3_out1);
  Multiplexer #(.width(32), .enable("false")) multiplexer_3 (
    .in0(c), .in1(c___1_t), .out(multiplexer_3_out), .sel(Write_ASCII));
  Comparator #(.width(32), .mode("unsigned")) comparator_1 (.a({32{1'b0}}), .b(n), .lt(_0_n));  // open: gt, eq
  Comparator #(.width(32), .mode("unsigned")) comparator_2 (.a({32{1'b0}}), .b(c), .lt(_0_c));  // open: gt, eq
  D_Flip_Flop IDLE_3 (.clk(CLK), .D(Write_ASCII), .Q(IDLE_3_q), .reset(RST));  // open: Qn, preset, en
  Demultiplexer #(.enable("false")) demultiplexer_2 (
    .out0(demultiplexer_2_out0), .out1(demultiplexer_2_out1), .in(IDLE_3_q), .sel(_0_c));
  Bit_Extender #(.in_width(32), .out_width(24)) bit_extender_1 (.in(multiplexer_3_out), .out(bit_extender_1_out));
  D_Flip_Flop IDLE_4 (.clk(CLK), .D(Lc_0), .Q(IDLE_4_q), .reset(RST));  // open: Qn, preset, en
  or or_4 (Lc, Lc_0, Write_ASCII);
  or or_5 (Ln, Ln_0, Lc_0);
  Demultiplexer #(.enable("false")) demultiplexer_3 (
    .out0(demultiplexer_3_out0), .out1(demultiplexer_3_out1), .in(IDLE_4_q), .sel(_0_n));
  D_Flip_Flop IDLE_5 (.clk(CLK), .D(demultiplexer_2_out0), .Q(\end ), .reset(RST));  // open: Qn, preset, en
  MEMORY memory_1 (
    .DIR(bit_extender_1_out), .DATA_IN(n___10___48), .WRITE(Lc_0), .CLK(CLK), .CLR(RST),
    .DATA_OUT(memory_1_data_out));
  Bit_Extender #(.in_width(32), .out_width(7)) bit_extender_2 (.in(memory_1_data_out), .out(ASCII));

  // Other names for the same wires on the sheet: Lc_1 = Write_ASCII; Sc = Write_ASCII; Ln_1 = Lc_0; Sn = Lc_0;
  //   Write = Lc_0
endmodule

module PRINT_DEC (
  input  [31:0] num,
  input  start,
  input  CLK,
  input  RST,
  output [6:0] ASCII,
  output Write_ASCII,
  output END
);

  wire demultiplexer_1_out0, demultiplexer_1_out1, demultiplexer_2_out0, demultiplexer_3_out0, end_t,
       IDLE_3_q, IDLE_q, or_1_out, or_2_out, or_3_out, S_ASCII, startUDEC, Write_ASCII_1;
  wire [6:0] ASCII_t;
  wire [31:0] multiplexer_1_out, negator_1_out;

  or or_1 (or_1_out, demultiplexer_1_out0, END);
  Negator #(.width(32)) negator_1 (.in(num), .out(negator_1_out));
  D_Flip_Flop IDLE (.clk(CLK), .D(or_1_out), .Q(IDLE_q), .preset(RST));  // open: Qn, en, reset
  Demultiplexer #(.enable("false")) demultiplexer_1 (
    .out0(demultiplexer_1_out0), .out1(demultiplexer_1_out1), .in(IDLE_q), .sel(start));
  Multiplexer #(.width(32), .enable("false")) multiplexer_1 (
    .in0(num), .in1(negator_1_out), .out(multiplexer_1_out), .sel(num[31]));
  Demultiplexer #(.enable("false")) demultiplexer_2 (
    .out0(demultiplexer_2_out0), .out1(S_ASCII), .in(demultiplexer_1_out1), .sel(num[31]));
  or or_2 (or_2_out, demultiplexer_2_out0, S_ASCII);
  D_Flip_Flop IDLE_2 (.clk(CLK), .D(or_2_out), .Q(startUDEC), .reset(RST));  // open: Qn, preset, en
  PRINT_UDEC print_udec_1 (
    .num(multiplexer_1_out), .start(startUDEC), .CLK(CLK), .RST(RST), .ASCII(ASCII_t),
    .Write_ASCII(Write_ASCII_1), .\end (end_t));
  D_Flip_Flop IDLE_3 (.clk(CLK), .D(or_3_out), .Q(IDLE_3_q), .reset(RST));  // open: Qn, preset, en
  or or_3 (or_3_out, startUDEC, demultiplexer_3_out0);
  Demultiplexer #(.enable("false")) demultiplexer_3 (
    .out0(demultiplexer_3_out0), .out1(END), .in(IDLE_3_q), .sel(end_t));
  Multiplexer #(.width(7), .enable("false")) multiplexer_2 (
    .in0(ASCII_t), .in1(7'b0101101), .out(ASCII), .sel(S_ASCII));
  or or_4 (Write_ASCII, S_ASCII, Write_ASCII_1);

  // Other names for the same wires on the sheet: sign = num[31]; Write_ASCII_0 = S_ASCII
endmodule

module TEST_PRINT (
  input  [31:0] in_1,
  output out_2
);

  wire button_1_out, button_2_out, CLK, CLR, d_ff_1_q, Write_ASCII;
  wire [6:0] ASCII;

  Button button_1 (.out(button_1_out));
  Clock clock_1 (.out(CLK));
  D_Flip_Flop d_ff_1 (.clk(CLK), .D(1'b1), .Q(d_ff_1_q), .reset(button_1_out));  // open: Qn, preset, en
  D_Flip_Flop d_ff_2 (.clk(CLK), .D(d_ff_1_q), .Qn(CLR), .reset(button_1_out));  // open: Q, preset, en
  Button button_2 (.out(button_2_out));
  PRINT_UDEC print_udec_1 ();  // open: num, start, CLK, RST, ASCII, Write_ASCII, end
  PRINT_DEC print_dec_1 (
    .num(in_1), .start(button_2_out), .CLK(CLK), .RST(CLR), .ASCII(ASCII), .Write_ASCII(Write_ASCII),
    .END(out_2));
  TTY #(.rows(32), .cols(60)) tty_1 (.data(ASCII), .clk(CLK), .we(Write_ASCII), .clr(CLR));
endmodule

module Control_Unit (
  input  in_1,
  input  in_2,
  input  in_3,
  input  in_4,
  output out_5,
  output out_6,
  output [6:0] ASCII
);

  wire d_ff_1_q, demultiplexer_1_out0, demultiplexer_1_out1, demultiplexer_2_out0, or_2_out, S;

  D_Flip_Flop d_ff_1 (.clk(in_1), .D(demultiplexer_1_out0), .Q(d_ff_1_q), .preset(in_3));  // open: Qn, en, reset
  Demultiplexer #(.enable("false")) demultiplexer_1 (
    .out0(demultiplexer_1_out0), .out1(demultiplexer_1_out1), .in(d_ff_1_q), .sel(in_2));
  Demultiplexer #(.enable("false")) demultiplexer_2 (
    .out0(demultiplexer_2_out0), .out1(S), .in(demultiplexer_1_out1), .sel(in_4));
  or or_1 (out_6, demultiplexer_2_out0, S);
  or or_2 (or_2_out, out_5, out_6);
  D_Flip_Flop d_ff_2 (.clk(in_1), .D(or_2_out), .Q(out_5), .reset(in_3));  // open: Qn, preset, en
  Multiplexer #(.width(7), .enable("false")) multiplexer_1 (.in0(7'b1000110), .in1(7'b1010100), .out(ASCII), .sel(S));

  // Other names for the same wires on the sheet: CLK = in_1; end = out_5; Paralelas = in_4; rst = in_3; start = in_2;
  //   write = out_6

  // Notes on the sheet:
  //   False
  //   True
endmodule

module DATA_PATH (
  input  in_1,
  input  in_2,
  input  in_3,
  input  in_4,
  input  in_5,
  input  in_6,
  input  in_7,
  input  in_8,
  input  in_9,
  input  in_10,
  input  [31:0] Memory_Input,
  output Paralelas
);

  wire dx1_0, dx1_0__dx2_0, dx1_0__dx2_0_t, dx2_0, dy1_dx1_dy2_dx2;
  wire [31:0] dx1, dx2, dy1, dy1_dx1, dy2, dy2_dx2, x11, x12, x21, x22, y11, y12, y21, y22;

  Register #(.width(32)) register_1 (.D(Memory_Input), .en(in_3), .Q(x11), .clk(in_1), .clr(in_2));
  Register #(.width(32)) register_2 (.D(Memory_Input), .en(in_5), .Q(x12), .clk(in_1), .clr(in_2));
  Register #(.width(32)) register_3 (.D(Memory_Input), .en(in_7), .Q(x21), .clk(in_1), .clr(in_2));
  Register #(.width(32)) register_4 (.D(Memory_Input), .en(in_9), .Q(x22), .clk(in_1), .clr(in_2));
  Register #(.width(32)) register_5 (.D(Memory_Input), .en(in_4), .Q(y11), .clk(in_1), .clr(in_2));
  Register #(.width(32)) register_6 (.D(Memory_Input), .en(in_6), .Q(y12), .clk(in_1), .clr(in_2));
  Register #(.width(32)) register_7 (.D(Memory_Input), .en(in_8), .Q(y21), .clk(in_1), .clr(in_2));
  Register #(.width(32)) register_8 (.D(Memory_Input), .en(in_10), .Q(y22), .clk(in_1), .clr(in_2));
  or or_1 (Paralelas, dy1_dx1_dy2_dx2, dx1_0__dx2_0);
  Subtractor #(.width(32)) subtractor_1 (.a(x11), .b(x12), .out(dx1));  // open: bin, bout
  Subtractor #(.width(32)) subtractor_2 (.a(x21), .b(x22), .out(dx2));  // open: bin, bout
  Subtractor #(.width(32)) subtractor_3 (.a(y11), .b(y12), .out(dy1));  // open: bin, bout
  Subtractor #(.width(32)) subtractor_4 (.a(y21), .b(y22), .out(dy2));  // open: bin, bout
  Divider #(.width(32)) divider_1 (.a(dy1), .b(dx1), .out(dy1_dx1), .upper({32{1'b0}}));  // open: rem
  Divider #(.width(32)) divider_2 (.a(dy2), .b(dx2), .out(dy2_dx2), .upper({32{1'b0}}));  // open: rem
  Comparator #(.width(32), .mode("unsigned")) comparator_1 (.a(dx1), .b({32{1'b0}}), .eq(dx1_0));  // open: gt, lt
  Comparator #(.width(32), .mode("unsigned")) comparator_2 (.a(dx2), .b({32{1'b0}}), .eq(dx2_0));  // open: gt, lt
  Comparator #(.width(32), .mode("unsigned")) comparator_3 (
    .a(dy1_dx1), .b(dy2_dx2), .eq(dy1_dx1_dy2_dx2));  // open: gt, lt
  or or_2 (dx1_0__dx2_0_t, dx1_0, dx2_0);
  and and_1 (dx1_0__dx2_0, dx1_0, dx2_0);

  // Other names for the same wires on the sheet: CLK = in_1; In[31:0] = Memory_Input; Lx11 = in_3; Lx12 = in_5;
  //   Lx21 = in_7; Lx22 = in_9; Ly11 = in_4; Ly12 = in_6; Ly21 = in_8; Ly22 = in_10; rst = in_2

  // Notes on the sheet:
  //   Coordenadas
  //   Loads
endmodule

module ASM (
  input  in_1,
  input  in_2,
  input  [31:0] Data_Input,
  output [23:0] out_4,
  output out_5,
  output [6:0] out_6,
  output out_7
);

  wire data_path_1_paralelas, loader_1_lx11, loader_1_lx12, loader_1_lx21, loader_1_lx22, loader_1_ly11,
       loader_1_ly12, loader_1_ly21, loader_1_ly22, loader_1_startcu;

  Loader loader_1 (
    .in_1(in_1), .in_2(in_2), .ReadAddress(out_4), .StartCu(loader_1_startcu), .Lx11(loader_1_lx11),
    .Ly11(loader_1_ly11), .Lx12(loader_1_lx12), .Ly12(loader_1_ly12), .Lx21(loader_1_lx21),
    .Ly21(loader_1_ly21), .Lx22(loader_1_lx22), .Ly22(loader_1_ly22));
  DATA_PATH data_path_1 (
    .in_2(in_2), .in_3(loader_1_lx11), .in_4(loader_1_ly11), .in_5(loader_1_lx12), .in_6(loader_1_ly12),
    .in_7(loader_1_lx21), .in_8(loader_1_ly21), .in_9(loader_1_lx22), .in_10(loader_1_ly22),
    .Paralelas(data_path_1_paralelas), .in_1(in_1), .Memory_Input(Data_Input));
  Control_Unit control_unit_1 (
    .in_2(loader_1_startcu), .in_3(in_2), .in_1(in_1), .out_5(out_5), .in_4(data_path_1_paralelas),
    .out_6(out_7), .ASCII(out_6));

  // Other names for the same wires on the sheet: CLK = in_1; RST = in_2
endmodule

module Loader (
  input  in_1,
  input  in_2,
  output [23:0] ReadAddress,
  output Lx11,
  output Lx12,
  output Lx21,
  output Lx22,
  output StartCu,
  output Ly11,
  output Ly12,
  output Ly21,
  output Ly22
);

  wire bit0, bit1, bit2, or_4_out;

  D_Flip_Flop d_ff_1 (.clk(in_1), .D(1'b0), .Q(Lx11), .preset(in_2));  // open: Qn, en, reset
  or or_1 (bit0, Ly11, Ly12, Ly21, Ly22);
  or or_2 (bit1, Lx12, Ly12, Lx22, Ly22);
  or or_3 (bit2, Lx21, Ly21, Lx22, Ly22);
  Multiplexer #(.select(3), .width(24), .enable("false")) multiplexer_1 (
    .in0({24{1'b0}}), .in1(24'h1), .in2(24'h2), .in3(24'h3), .in4(24'h4), .in5(24'h5), .in6(24'h6),
    .in7(24'h7), .out(ReadAddress), .sel({bit2, bit1, bit0}));
  D_Flip_Flop Wait (.clk(in_1), .D(Lx11), .Q(Ly11), .reset(in_2));  // open: Qn, preset, en
  D_Flip_Flop Wait_2 (.clk(in_1), .D(Ly11), .Q(Lx12), .reset(in_2));  // open: Qn, preset, en
  D_Flip_Flop Wait_3 (.clk(in_1), .D(Lx12), .Q(Ly12), .reset(in_2));  // open: Qn, preset, en
  D_Flip_Flop Wait_4 (.clk(in_1), .D(Ly12), .Q(Lx21), .reset(in_2));  // open: Qn, preset, en
  D_Flip_Flop Wait_5 (.clk(in_1), .D(Lx21), .Q(Ly21), .reset(in_2));  // open: Qn, preset, en
  D_Flip_Flop Wait_6 (.clk(in_1), .D(Ly21), .Q(Lx22), .reset(in_2));  // open: Qn, preset, en
  D_Flip_Flop Wait_7 (.clk(in_1), .D(Lx22), .Q(Ly22), .reset(in_2));  // open: Qn, preset, en
  or or_4 (or_4_out, StartCu, Ly22);
  D_Flip_Flop End (.clk(in_1), .D(or_4_out), .Q(StartCu), .reset(in_2));  // open: Qn, preset, en

  // Other names for the same wires on the sheet: CLK = in_1; RST = in_2; Saddress[2:0] = {bit2, bit1, bit0};
  //   T1 = Lx11; T2 = Ly11; T3 = Lx12; T4 = Ly12; T5 = Lx21; T6 = Ly21; T7 = Lx22; T8 = Ly22
endmodule
